# Fritzing sketch Rocket (saved by Fritzing 1.0.3b)
breadboards: 1

parts:
  Pico_H1 = Raspberry Pi Pico H
  433T30D1 = 433T30D
  A1 = NEO-6M GPS Module [part_number=GY-GPS6MV2]
  Part1 = DFROBOT_Intelligent_10DOF_AHRS_v1.0
  SD_card_module1 = SD Card Module

nets:
  GND: Pico_H1.GND, 433T30D1.M0, 433T30D1.M1, 433T30D1.GND, SD_card_module1.GND#0
  VCC: Pico_H1.3V3, 433T30D1.VCC, A1.Vcc, SD_card_module1.+3.3
  N1: Pico_H1.GP19, SD_card_module1.MOSI
  N2: Pico_H1.GP18, SD_card_module1.SCK
  N3: Pico_H1.GP17, SD_card_module1.CS
  N4: Pico_H1.GP16, SD_card_module1.MISO
  N5: Pico_H1.GP9, A1.Tx
  N6: Pico_H1.GP8, A1.Rx
  N7: Pico_H1.GP5, Part1.SCL
  N8: Pico_H1.GP4, Part1.SDA
  N9: Pico_H1.GP1, 433T30D1.TXD
  N10: Pico_H1.GP0, 433T30D1.RXD

custom parts:
  Raspberry Pi Pico H: Raspberry Pi Pico H. Based around the RP2040 microcontroller the Pico H is a low cost microcontroller device bringing Raspberry Pi quality, cost, and easy of use to the microcontroller space.
  433T30D: Long Distance Wireless Transceiver UART LoRa Module
  NEO-6M GPS Module: GY-GPS6MV2 NEO-6M GPS Module Module based on U-blox NEO-6M GPS engine, incorporating regulator for 3.3-5V DC input, MS621FE-compatible rechargeable battery for backup and EEPROM for storing configuration settings. Links: NEO-6 series product information page NEO-6 Datasheet
  DFROBOT_Intelligent_10DOF_AHRS_v1.0: A DIP stand-in part for whatever IC you want. With 10 pins on a 300mil dual inline package (DIP) footprint. I couldn't build PCB design. So there are only Breadborad and Schematic design. https://www.dfrobot.com/product-1793.html https://wiki.dfrobot.com/Gravity_BNO055_+_BMP280%20intelligent_10DOF_AHRS_SKU_SEN0253#target_3
  SD Card Module: SD Card Module Slot Socket Reader For Arduino ARM MCU
